// Logisim project cpu.circ as structural Verilog: 13 circuits, main circuit main
module main (
  input  E,
  input  E_AC_0,
  input  [3:0] INPR,
  input  E_AC_3,
  output Cout
);

  wire and_1_out, clock_1_out, main_controller_1_ac_bus, main_controller_1_ac_clr, main_controller_1_ac_inc,
       main_controller_1_ac_load, main_controller_1_add, main_controller_1_and, main_controller_1_ar_bus,
       main_controller_1_ar_inc, main_controller_1_ar_ld, main_controller_1_cil, main_controller_1_cir,
       main_controller_1_cma, main_controller_1_dr_load, main_controller_1_hlt, main_controller_1_ir_bus,
       main_controller_1_ir_load, main_controller_1_ld_inpr, main_controller_1_ld_outr,
       main_controller_1_memory_bus, main_controller_1_memory_load, main_controller_1_pc_bus,
       main_controller_1_pc_inc, main_controller_1_pc_ld, not_1_out;
  wire [3:0] AC_output, alu_4_1_output_ac, AR_output, controlled_buffer_1_out, controlled_buffer_1_out_2,
       DR_output, IR_output, IR_output_2, OUTR_output, PC_output;
  wire [7:0] ram_1_data;

  main_controller main_controller_1 (
    .CLK(and_1_out), .ir_4_7(IR_output_2), .pc_ld(main_controller_1_pc_ld),
    .pc_inc(main_controller_1_pc_inc), .pc_bus(main_controller_1_pc_bus), .HLT(main_controller_1_hlt),
    .ar_ld(main_controller_1_ar_ld), .ar_inc(main_controller_1_ar_inc), .ar_bus(main_controller_1_ar_bus),
    .memory_load(main_controller_1_memory_load), .memory_bus(main_controller_1_memory_bus),
    .dr_load(main_controller_1_dr_load), .ir_load(main_controller_1_ir_load),
    .ir_bus(main_controller_1_ir_bus), .ac_load(main_controller_1_ac_load),
    .ac_bus(main_controller_1_ac_bus), .ac_clr(main_controller_1_ac_clr), .ac_inc(main_controller_1_ac_inc),
    .\and (main_controller_1_and), .add(main_controller_1_add), .cir(main_controller_1_cir),
    .cma(main_controller_1_cma), .cil(main_controller_1_cil), .ld_inpr(main_controller_1_ld_inpr),
    .ld_outr(main_controller_1_ld_outr));
  and and_1 (and_1_out, clock_1_out, not_1_out);
  not not_1 (not_1_out, main_controller_1_hlt);
  // Probe on alu_4_1_output_ac
  ALU_4 alu_4_1 (
    .AC(AC_output), .DR(DR_output), .INPR(INPR), .AND(main_controller_1_and), .ADD(main_controller_1_add),
    .CMA(main_controller_1_cma), .LD_DR(main_controller_1_dr_load), .LD_INPR(main_controller_1_ld_inpr),
    .CIR(main_controller_1_cir), .CIL(main_controller_1_cil), .Cin(E), .E_AC_0(E_AC_0), .Cout(E_AC_3),
    .E_AC_3(E_AC_3), .OUTPUT_AC(alu_4_1_output_ac));
  RAM #(.addrWidth(4), .bus("separate")) ram_1 (
    .addr(AR_output), .din({controlled_buffer_1_out_2, controlled_buffer_1_out}), .data(ram_1_data),
    .str(main_controller_1_memory_load), .clk(clock_1_out));  // open: sel, ld, clr
  reg_4 AR (
    .INPUT(controlled_buffer_1_out), .CLK(clock_1_out), .INC(main_controller_1_ar_inc),
    .LD(main_controller_1_ar_ld), .OUTPUT(AR_output));  // open: CLR
  // Probe on AR_output
  reg_4 PC (
    .INPUT(controlled_buffer_1_out), .CLK(clock_1_out), .INC(main_controller_1_pc_inc),
    .LD(main_controller_1_pc_ld), .OUTPUT(PC_output));  // open: CLR
  // Probe on PC_output
  reg_4 DR (
    .INPUT(controlled_buffer_1_out), .CLK(clock_1_out), .LD(main_controller_1_dr_load), .OUTPUT(DR_output));  // open: INC, CLR
  reg_4 AC (
    .INPUT(alu_4_1_output_ac), .CLK(clock_1_out), .INC(main_controller_1_ac_inc),
    .LD(main_controller_1_ac_load), .CLR(main_controller_1_ac_clr), .OUTPUT(AC_output));
  // Probe on AC_output
  // Probe on {IR_output_2, IR_output}
  reg_8 IR (
    .INPUT({controlled_buffer_1_out_2, controlled_buffer_1_out}), .CLK(clock_1_out),
    .LD(main_controller_1_ir_load), .OUTPUT({IR_output_2, IR_output}));
  reg_4 OUTR (
    .INPUT(controlled_buffer_1_out), .CLK(clock_1_out), .LD(main_controller_1_ld_outr), .OUTPUT(OUTR_output));  // open: INC, CLR
  Clock clock_1 (.out(clock_1_out));
  // Probe on DR_output
  // Probe on OUTR_output
  assign {controlled_buffer_1_out_2, controlled_buffer_1_out} = main_controller_1_memory_bus ? ram_1_data : 8'bz;  // Controlled_Buffer controlled_buffer_1
  assign {controlled_buffer_1_out_2, controlled_buffer_1_out} = main_controller_1_ar_bus ? {4'b0000, AR_output} : 8'bz;  // Controlled_Buffer controlled_buffer_2
  assign {controlled_buffer_1_out_2, controlled_buffer_1_out} = main_controller_1_pc_bus ? {4'b0000, PC_output} : 8'bz;  // Controlled_Buffer controlled_buffer_3
  assign {controlled_buffer_1_out_2, controlled_buffer_1_out} = main_controller_1_ac_bus ? {4'b0000, AC_output} : 8'bz;  // Controlled_Buffer controlled_buffer_4
  assign {controlled_buffer_1_out_2, controlled_buffer_1_out} = main_controller_1_ir_bus ? {IR_output_2, IR_output} : 8'bz;  // Controlled_Buffer controlled_buffer_5

  assign Cout = E_AC_3;
endmodule

module reg_4 (
  input  INC,
  input  LD,
  input  [3:0] INPUT,
  input  CLK,
  input  CLR,
  output [3:0] OUTPUT
);

  wire and_1_out, and_2_out, and_3_out, and_4_out, and_5_out, and_6_out, and_7_out, and_8_out, and_9_out,
       and_10_out, and_11_out, and_12_out, not_1_out, not_2_out, not_3_out, not_4_out, not_5_out, or_1_out,
       or_2_out, or_3_out, or_4_out, or_5_out, or_6_out, or_7_out, or_8_out;

  not not_1 (not_1_out, LD);
  and and_1 (and_1_out, INC, not_1_out);
  not not_2 (not_2_out, INPUT[0]);
  not not_3 (not_3_out, INPUT[1]);
  not not_4 (not_4_out, INPUT[2]);
  not not_5 (not_5_out, INPUT[3]);
  and and_2 (and_2_out, LD, INPUT[0]);
  and and_3 (and_3_out, LD, not_2_out);
  and and_4 (and_4_out, LD, INPUT[1]);
  and and_5 (and_5_out, LD, not_3_out);
  and and_6 (and_6_out, LD, INPUT[2]);
  and and_7 (and_7_out, LD, not_4_out);
  and and_8 (and_8_out, LD, INPUT[3]);
  and and_9 (and_9_out, LD, not_5_out);
  and and_10 (and_10_out, OUTPUT[0], and_1_out);
  and and_11 (and_11_out, OUTPUT[1], OUTPUT[0], and_1_out);
  and and_12 (and_12_out, OUTPUT[2], OUTPUT[1], OUTPUT[0], and_1_out);
  or or_1 (or_1_out, and_2_out, and_1_out);
  or or_2 (or_2_out, and_3_out, and_1_out);
  or or_3 (or_3_out, and_4_out, and_10_out);
  or or_4 (or_4_out, and_5_out, and_10_out);
  or or_5 (or_5_out, and_6_out, and_11_out);
  or or_6 (or_6_out, and_7_out, and_11_out);
  or or_7 (or_7_out, and_8_out, and_12_out);
  or or_8 (or_8_out, and_9_out, and_12_out);
  J_K_Flip_Flop j_k_ff_1 (.J(or_1_out), .clk(CLK), .K(or_2_out), .Q(OUTPUT[0]), .reset(CLR));  // open: Qn, preset, en
  J_K_Flip_Flop j_k_ff_2 (.J(or_3_out), .clk(CLK), .K(or_4_out), .Q(OUTPUT[1]), .reset(CLR));  // open: Qn, preset, en
  J_K_Flip_Flop j_k_ff_3 (.J(or_5_out), .clk(CLK), .K(or_6_out), .Q(OUTPUT[2]), .reset(CLR));  // open: Qn, preset, en
  J_K_Flip_Flop j_k_ff_4 (.J(or_7_out), .clk(CLK), .K(or_8_out), .Q(OUTPUT[3]), .reset(CLR));  // open: Qn, preset, en
endmodule

module reg_8 (
  input  [7:0] INPUT,
  input  CLK,
  input  LD,
  output [7:0] OUTPUT
);

  reg_4 REG_4 (.INPUT(INPUT[3:0]), .CLK(CLK), .LD(LD), .OUTPUT(OUTPUT[3:0]));  // open: INC, CLR
  reg_4 REG_4_2 (.INPUT(INPUT[7:4]), .CLK(CLK), .LD(LD), .OUTPUT(OUTPUT[7:4]));  // open: INC, CLR
endmodule

module ALU_1 (
  input  INPR,
  input  DR,
  input  AC,
  input  AND,
  input  Cin,
  input  ADD,
  input  CMA,
  input  LD_DR,
  input  LD_INPR,
  input  CIR,
  input  CIL,
  input  AC_i_1,
  input  AC_i_1_2,
  output Cout,
  output OUTPUT_AC
);

  wire ADD_out, adder_1_out, AND_out, COMP_out, ID_DR_out, ID_INPR_out, not_1_out, SHL_out, SHR_out;

  Adder #(.width(1)) adder_1 (.a(AC), .b(DR), .out(adder_1_out), .cin(Cin), .cout(Cout));
  not not_1 (not_1_out, AC);
  and u_AND (AND_out, AND, AC, DR);
  and u_ADD (ADD_out, ADD, adder_1_out);
  and COMP (COMP_out, CMA, not_1_out);
  and ID_DR (ID_DR_out, LD_DR, DR);
  and ID_INPR (ID_INPR_out, LD_INPR, INPR);
  and SHR (SHR_out, CIR, AC_i_1_2);
  and SHL (SHL_out, CIL, AC_i_1);
  or or_1 (OUTPUT_AC, AND_out, ADD_out, COMP_out, ID_DR_out, ID_INPR_out, SHR_out, SHL_out);
endmodule

// ALU
module ALU_4 (
  input  Cin,
  input  E_AC_0,
  input  [3:0] AC,
  input  [3:0] DR,
  input  [3:0] INPR,
  input  AND,
  input  ADD,
  input  CMA,
  input  LD_DR,
  input  LD_INPR,
  input  CIR,
  input  CIL,
  input  E_AC_3,
  output [3:0] OUTPUT_AC,
  output Cout
);

  wire AC_0_cout, AC_1_cout, AC_2_cout;

  ALU_1 AC_0 (
    .AND(AND), .ADD(ADD), .CMA(CMA), .LD_DR(LD_DR), .LD_INPR(LD_INPR), .CIR(CIR), .CIL(CIL), .AC_i_1(E_AC_0),
    .AC_i_1_2(AC[1]), .INPR(INPR[0]), .DR(DR[0]), .AC(AC[0]), .Cin(Cin), .Cout(AC_0_cout),
    .OUTPUT_AC(OUTPUT_AC[0]));
  ALU_1 AC_1 (
    .AND(AND), .ADD(ADD), .CMA(CMA), .LD_DR(LD_DR), .LD_INPR(LD_INPR), .CIR(CIR), .CIL(CIL), .AC_i_1(AC[0]),
    .AC_i_1_2(AC[2]), .INPR(INPR[1]), .DR(DR[1]), .AC(AC[1]), .Cin(AC_0_cout), .Cout(AC_1_cout),
    .OUTPUT_AC(OUTPUT_AC[1]));
  ALU_1 AC_2 (
    .AND(AND), .ADD(ADD), .CMA(CMA), .LD_DR(LD_DR), .LD_INPR(LD_INPR), .CIR(CIR), .CIL(CIL), .AC_i_1(AC[1]),
    .AC_i_1_2(AC[3]), .INPR(INPR[2]), .DR(DR[2]), .AC(AC[2]), .Cin(AC_1_cout), .Cout(AC_2_cout),
    .OUTPUT_AC(OUTPUT_AC[2]));
  ALU_1 AC_3 (
    .AND(AND), .ADD(ADD), .CMA(CMA), .LD_DR(LD_DR), .LD_INPR(LD_INPR), .CIR(CIR), .CIL(CIL), .AC_i_1(AC[2]),
    .AC_i_1_2(E_AC_3), .INPR(INPR[3]), .DR(DR[3]), .AC(AC[3]), .Cin(AC_2_cout), .Cout(Cout),
    .OUTPUT_AC(OUTPUT_AC[3]));
endmodule

module control_dr (
  input  T3,
  input  D0,
  input  D1,
  input  D2,
  output DR_ld
);

  wire or_1_out;

  or or_1 (or_1_out, D2, D1, D0);
  and and_1 (DR_ld, or_1_out, T3);
endmodule

module control_ar (
  input  T0,
  input  T2,
  input  T3,
  input  T4,
  input  D4,
  input  D5,
  output AR_ld,
  output AR_inc,
  output AR_bus
);

  wire and_1_out, and_2_out;

  and and_1 (and_1_out, D5, T4);
  and and_2 (and_2_out, D4, T3);
  and and_3 (AR_inc, D5, T3);
  or or_1 (AR_ld, T2, T0);
  or or_2 (AR_bus, and_1_out, and_2_out);
endmodule

module control_sc (
  input  T3,
  input  T4,
  input  D0,
  input  D1,
  input  D2,
  input  D3,
  input  D4,
  input  D5,
  input  D6,
  input  D7,
  input  D8,
  input  D9,
  input  D10,
  input  D11,
  input  D12,
  input  D13,
  input  D14,
  input  D15,
  output SC_clr
);

  wire and_1_out, and_2_out, or_1_out, or_2_out;

  or or_1 (or_1_out, D5, D2, D1, D0);
  or or_2 (or_2_out, D15, D14, D13, D12, D11, D10, D9, D8, D7, D6, D4, D3);
  and and_1 (and_1_out, or_1_out, T4);
  and and_2 (and_2_out, or_2_out, T3);
  or or_3 (SC_clr, and_1_out, and_2_out);
endmodule

module control_pc (
  input  T0,
  input  T1,
  input  T3,
  input  T4,
  input  D4,
  input  D5,
  input  D6,
  output PC_ld,
  output PC_inc,
  output PC_bus
);

  wire and_1_out, and_2_out, and_3_out, or_1_out;

  or or_1 (or_1_out, D6, D4);
  and and_1 (and_1_out, or_1_out, T3);
  and and_2 (and_2_out, D5, T4);
  and and_3 (and_3_out, D5, T3);
  or or_2 (PC_ld, and_1_out, and_2_out);
  or or_3 (PC_bus, and_3_out, T0);

  assign PC_inc = T1;
endmodule

// AC_ld
module control_ac (
  input  T3,
  input  T4,
  input  D0,
  input  D1,
  input  D2,
  input  D3,
  input  D7,
  input  D9,
  input  D10,
  input  D11,
  input  D12,
  input  D13,
  input  D14,
  output AC_load,
  output AC_bus,
  output AC_and,
  output AC_add,
  output cir,
  output cma,
  output cil,
  output AC_clr,
  output AC_inc,
  output ld_inpr,
  output ld_outr
);

  wire and_1_out, and_2_out, and_5_out;

  and and_1 (and_1_out, D1, T4);
  and and_2 (and_2_out, D2, T4);
  and and_3 (AC_and, D0, T4);
  and and_4 (ld_outr, D14, T3);
  and and_5 (and_5_out, D3, T3);
  or or_1 (AC_add, and_2_out, and_1_out);
  and and_6 (cir, D11, T3);
  and and_7 (cma, D9, T3);
  and and_8 (cil, D12, T3);
  and and_9 (AC_clr, D7, T3);
  and and_10 (AC_inc, D10, T3);
  and and_11 (ld_inpr, D13, T3);
  or or_2 (AC_load, and_1_out, and_2_out, AC_and, ld_inpr);
  or or_3 (AC_bus, ld_outr, and_5_out);
endmodule

module control_memory (
  input  T1,
  input  T3,
  input  D0,
  input  D1,
  input  D2,
  input  D3,
  input  D5,
  input  D6,
  output memory_ld,
  output memory_bus
);

  wire and_2_out, or_1_out, or_2_out;

  or or_1 (or_1_out, D5, D3);
  or or_2 (or_2_out, D6, D2, D1, D0);
  and and_1 (memory_ld, or_1_out, T3);
  and and_2 (and_2_out, or_2_out, T3);
  or or_3 (memory_bus, and_2_out, T1);
endmodule

module control_ir (
  input  T1,
  input  T2,
  output ir_load,
  output ir_bus
);


  assign ir_bus = T2;
  assign ir_load = T1;
endmodule

module main_controller (
  input  CLK,
  input  [3:0] ir_4_7,
  output pc_ld,
  output pc_inc,
  output pc_bus,
  output HLT,
  output ar_ld,
  output ar_inc,
  output ar_bus,
  output memory_load,
  output memory_bus,
  output dr_load,
  output ir_load,
  output ir_bus,
  output ac_load,
  output ac_bus,
  output ac_clr,
  output ac_inc,
  output \and ,
  output add,
  output cir,
  output cma,
  output cil,
  output ld_inpr,
  output ld_outr
);

  wire control_sc_1_sc_clr, d_ff_1_q, decoder_1_out0, decoder_1_out1, decoder_1_out2, decoder_1_out3,
       decoder_1_out4;
  wire [1:0] decoder_2_out5;
  wire [3:0] counter_1_q;
  wire [10:0] decoder_2_out0;
  wire [15:4] decoder_2_out4;

  Decoder #(.select(4)) decoder_1 (
    .out0(decoder_1_out0), .out1(decoder_1_out1), .out2(decoder_1_out2), .out3(decoder_1_out3),
    .out4(decoder_1_out4), .sel(counter_1_q));  // open: out5, out6, out7, out8, out9, out10, out11, out12, out13, out14, out15, en
  Counter #(.width(4), .max('hf)) counter_1 (
    .Q(counter_1_q), .clk(CLK), .clr(d_ff_1_q));  // open: load, D, count, carry
  D_Flip_Flop d_ff_1 (.clk(CLK), .D(control_sc_1_sc_clr), .Q(d_ff_1_q));  // open: Qn, preset, en, reset
  Decoder #(.select(4)) decoder_2 (
    .out0(decoder_2_out0[10]), .out1(decoder_2_out0[9]), .out2(decoder_2_out0[8]), .out3(decoder_2_out0[7]),
    .out4(decoder_2_out4[4]), .out5(decoder_2_out5[1]), .out6(decoder_2_out5[0]), .out7(decoder_2_out0[6]),
    .out8(decoder_2_out4[8]), .out9(decoder_2_out0[5]), .out10(decoder_2_out0[4]), .out11(decoder_2_out0[3]),
    .out12(decoder_2_out0[2]), .out13(decoder_2_out0[1]), .out14(decoder_2_out0[0]),
    .out15(decoder_2_out4[15]), .sel(ir_4_7));  // open: en
  control_ar control_ar_1 (
    .T0(decoder_1_out0), .T2(decoder_1_out2), .T3(decoder_1_out3), .T4(decoder_1_out4),
    .D4(decoder_2_out4[4]), .D5(decoder_2_out5[1]), .AR_ld(ar_ld), .AR_inc(ar_inc), .AR_bus(ar_bus));
  control_dr control_dr_1 (
    .T3(decoder_1_out3), .D0(decoder_2_out0[10]), .D1(decoder_2_out0[9]), .D2(decoder_2_out0[8]),
    .DR_ld(dr_load));
  control_ir control_ir_1 (.T1(decoder_1_out1), .T2(decoder_1_out2), .ir_load(ir_load), .ir_bus(ir_bus));
  control_pc control_pc_1 (
    .T0(decoder_1_out0), .T1(decoder_1_out1), .T3(decoder_1_out3), .T4(decoder_1_out4),
    .D4(decoder_2_out4[4]), .D5(decoder_2_out5[1]), .D6(decoder_2_out5[0]), .PC_ld(pc_ld), .PC_inc(pc_inc),
    .PC_bus(pc_bus));
  control_memory control_memory_1 (
    .T1(decoder_1_out1), .T3(decoder_1_out3), .D0(decoder_2_out0[10]), .D1(decoder_2_out0[9]),
    .D2(decoder_2_out0[8]), .D3(decoder_2_out0[7]), .D5(decoder_2_out5[1]), .D6(decoder_2_out5[0]),
    .memory_ld(memory_load), .memory_bus(memory_bus));
  control_ac control_ac_1 (
    .T3(decoder_1_out3), .T4(decoder_1_out4), .D0(decoder_2_out0[10]), .D1(decoder_2_out0[9]),
    .D2(decoder_2_out0[8]), .D3(decoder_2_out0[7]), .D7(decoder_2_out0[6]), .D9(decoder_2_out0[5]),
    .D10(decoder_2_out0[4]), .D11(decoder_2_out0[3]), .D12(decoder_2_out0[2]), .D13(decoder_2_out0[1]),
    .D14(decoder_2_out0[0]), .AC_load(ac_load), .AC_bus(ac_bus), .AC_and(\and ), .AC_add(add), .cir(cir),
    .cma(cma), .cil(cil), .AC_clr(ac_clr), .AC_inc(ac_inc), .ld_inpr(ld_inpr), .ld_outr(ld_outr));
  control_sc control_sc_1 (
    .T3(decoder_1_out3), .T4(decoder_1_out4), .D0(decoder_2_out0[10]), .D1(decoder_2_out0[9]),
    .D2(decoder_2_out0[8]), .D3(decoder_2_out0[7]), .D4(decoder_2_out4[4]), .D5(decoder_2_out5[1]),
    .D6(decoder_2_out5[0]), .D7(decoder_2_out0[6]), .D8(decoder_2_out4[8]), .D9(decoder_2_out0[5]),
    .D10(decoder_2_out0[4]), .D11(decoder_2_out0[3]), .D12(decoder_2_out0[2]), .D13(decoder_2_out0[1]),
    .D14(decoder_2_out0[0]), .D15(decoder_2_out4[15]), .SC_clr(control_sc_1_sc_clr));
  and and_1 (HLT, decoder_1_out3, decoder_2_out4[15]);
endmodule
